# Fritzing sketch Diagrama (saved by Fritzing 0.9.9b)
breadboards: 1

parts:
  HC-05 = Bluetooth HC-05 Macho
  9V = BC9VPC [package=bc9vpc]
  Arduino = Arduino Uno (Rev3)
  U1 = 7-Segment-Display-4-Red [part_number=3461AS package="7-Segment-4 [THT]"]
  R1 = Resistor [tolerance=±5% resistance=330 package=THT]
  R2 = Resistor [tolerance=±5% resistance=330 package=THT]
  R3 = Resistor [tolerance=±5% resistance=330 package=THT]
  R4 = Resistor [tolerance=±5% resistance=330 package=THT]
  R5 = Resistor [tolerance=±5% resistance=330 package=THT]
  R6 = Resistor [tolerance=±5% resistance=330 package=THT]
  R7 = Resistor [tolerance=±5% resistance=330 package=THT]
  R8 = Resistor [tolerance=±5% resistance=330 package=THT]
  J1 = Piezo Speaker
  LED1 = LED - 5mm [color="Red (633nm)" package="5 mm [THT]"]
  R9 = Resistor [tolerance=±5% resistance=330 package=THT]

nets:
  N1: HC-05.RXD, R8.Pin_0
  VCC: HC-05.VCC, Arduino.5V
  GND: HC-05.GND, 9V.V-, Arduino.GND, J1.pin1, R9.Pin_1
  N2: 9V.V+, Arduino.VIN
  N3: Arduino.A0, J1.pin2
  N4: Arduino.D8, R4.Pin_0
  N5: Arduino.D9_PWM, R5.Pin_0
  N6: Arduino.D10_PWM/SS, R6.Pin_0
  N7: Arduino.D11_PWM/MOSI, R7.Pin_0
  N8: Arduino.D13/SCK, LED1.anode
  N9: Arduino.D1/TX, R8.Pin_1
  N10: Arduino.D2, U1.pin6
  N11: Arduino.D3_PWM, U1.pin8
  N12: Arduino.D4, U1.pin_9
  N13: Arduino.D5_PWM, R1.Pin_0
  N14: Arduino.D6_PWM, R2.Pin_0
  N15: Arduino.D7, R3.Pin_0
  N16: U1.pin1, R3.Pin_1
  N17: U1.pin2, R4.Pin_1
  N18: U1.pin4, R5.Pin_1
  N19: U1.pin5, R1.Pin_1
  N20: U1.pin7, R6.Pin_1
  N21: U1.pin_10, R2.Pin_1
  N22: U1.pin_11, R7.Pin_1
  N23: LED1.cathode, R9.Pin_0

custom parts:
  7-Segment-Display-4-Red: 7-Segment Display 4 digits Red
